# Fritzing sketch pan-tilt-camera-wiring (saved by Fritzing 1.0.1rc)

parts:
  JACK1 = 2.1mm Barrel Jack with Terminal Block
  Mod1 = Raspberry Pi 4B
  J1 = Basic Servo
  J2 = Basic Servo
  J4 = Wago 221-415
  J5 = Wago 221-413

nets:
  VCC: JACK1.POS, J1.vcc, J2.vcc, J5.Pin_1, J5.Pin_2, J5.Pin_3
  GND: JACK1.NEG, Mod1.GND, J1.gnd, J2.gnd, J4.Pin_1, J4.Pin_2, J4.Pin_3, J4.Pin_4, J4.Pin_5
  N1: Mod1.GPIO14, J1.pulse
  N2: Mod1.GPIO15, J2.pulse

custom parts:
  Wago 221-415: Wago 221-415 5 position splicing connector 12AWG.
  Wago 221-413: Wago 221-413 3 position splicing connector 12AWG.
